// Logisim project LALU.circ as structural Verilog: 29 circuits, main circuit main
module main (
  input  rst
);

  wire addersubtractor_me_1_overflow, and_2_out, and_4_out, and_5_out, clk, d_ff_2_q, fv, irdecoder_1_halt,
       irdecoder_1_sub, jmp, jmp_priv, jmpn, ld, ldi, msb, mv, reg0WE, reg1WE, reg2WE, reg3WE, register_3_q,
       st;
  wire [1:0] IR_q, irdecoder_1_rd, irdecoder_1_rs;
  wire [2:0] addersubtractor_me_1_sum_4;
  wire [3:0] addersubtractor_me_1_sum, addersubtractor_me_1_sum_2, addersubtractor_me_1_sum_3;
  wire [5:0] pci, programcounter_1_pc;
  wire [6:0] RsLower;
  wire [7:0] bit_extender_1_out, ProgramMemory_dout, register_1_q, register_2_q;
  wire [15:0] bit_extender_2_out, cyclecounter_1_cycles, loadRes, R0, R1, R2, R3, Rd, Rs, Write;

  Clock u_clk (.out(clk));
  Register #(.width(16)) u_R0 (.D(Write), .en(reg0WE), .clk(clk), .Q(R0), .clr(rst));
  Register #(.width(16)) u_R1 (.D(Write), .en(reg1WE), .clk(clk), .Q(R1), .clr(rst));
  Register #(.width(16)) u_R2 (.D(Write), .en(reg2WE), .clk(clk), .Q(R2), .clr(rst));
  Register #(.width(16)) u_R3 (.D(Write), .en(reg3WE), .clk(clk), .Q(R3), .clr(rst));
  ProgramCounter programcounter_1 (
    .jmpn(jmpn), .jmp(jmp_priv), .neg(msb), .pci(pci), .clk(clk), .rst(rst), .pc(programcounter_1_pc));
  assign bit_extender_1_out = {{2{1'b0}}, programcounter_1_pc};  // Bit_Extender bit_extender_1
  RAM #(.addrWidth(6), .asyncread("true"), .trigger("falling")) ProgramMemory (
    .addr(programcounter_1_pc), .we(1'b0), .oe(1'b1), .clk(clk), .dout(ProgramMemory_dout));  // open: din
  RAM #(.addrWidth(7), .asyncread("true"), .dataWidth(16), .trigger("falling")) DataMemory (
    .addr(RsLower), .we(st), .oe(1'b1), .clk(clk), .din(Rd), .dout(loadRes));
  Hex_Digit_Display #(.decimalPoint("false")) hex_digit_display_1 (.value(R0[15:12]));
  Hex_Digit_Display #(.decimalPoint("false")) hex_digit_display_2 (.value(R0[11:8]));
  Hex_Digit_Display #(.decimalPoint("false")) hex_digit_display_3 (.value(R0[7:4]));
  Hex_Digit_Display #(.decimalPoint("false")) hex_digit_display_4 (.value(bit_extender_1_out[7:4]));
  Hex_Digit_Display #(.decimalPoint("false")) hex_digit_display_5 (.value(bit_extender_1_out[3:0]));
  Register IR (.D(ProgramMemory_dout), .en(1'b1), .clk(clk), .Q({pci, IR_q}), .clr(rst));
  Hex_Digit_Display #(.decimalPoint("false")) hex_digit_display_6 (.value(R0[3:0]));
  Hex_Digit_Display #(.decimalPoint("false")) hex_digit_display_7 (.value(R1[15:12]));
  Hex_Digit_Display #(.decimalPoint("false")) hex_digit_display_8 (.value(pci[5:2]));
  Hex_Digit_Display #(.decimalPoint("false")) hex_digit_display_9 (.value(R1[11:8]));
  Hex_Digit_Display #(.decimalPoint("false")) hex_digit_display_10 (.value(R1[7:4]));
  Register register_1 (.D({pci, IR_q}), .en(1'b1), .clk(clk), .Q(register_1_q), .clr(rst));
  Hex_Digit_Display #(.decimalPoint("false")) hex_digit_display_11 (.value({pci[1:0], IR_q}));
  Hex_Digit_Display #(.decimalPoint("false")) hex_digit_display_12 (.value(R1[3:0]));
  Hex_Digit_Display #(.decimalPoint("false")) hex_digit_display_13 (.value(register_1_q[7:4]));
  and and_1 (jmp_priv, ~IR_q[1], fv);  // AND_Gate
  Hex_Digit_Display #(.decimalPoint("false")) hex_digit_display_14 (.value(R2[15:12]));
  Hex_Digit_Display #(.decimalPoint("false")) hex_digit_display_15 (.value(R2[11:8]));
  Register register_2 (.D(register_1_q), .en(1'b1), .clk(clk), .Q(register_2_q), .clr(rst));
  Hex_Digit_Display #(.decimalPoint("false")) hex_digit_display_16 (.value(register_1_q[3:0]));
  and and_2 (and_2_out, ~IR_q[1], IR_q[0]);  // AND_Gate
  and and_3 (jmpn, and_2_out, fv);
  D_Flip_Flop d_ff_1 (.D(jmp_priv), .clk(clk), .Q(jmp), .reset(rst));  // open: Qn, preset
  Hex_Digit_Display #(.decimalPoint("false")) hex_digit_display_17 (.value(R2[7:4]));
  Hex_Digit_Display #(.decimalPoint("false")) hex_digit_display_18 (.value(R2[3:0]));
  Hex_Digit_Display #(.decimalPoint("false")) hex_digit_display_19 (.value(register_2_q[7:4]));
  D_Flip_Flop d_ff_2 (.D(1'b1), .clk(clk), .Q(d_ff_2_q), .reset(rst));  // open: Qn, preset
  Hex_Digit_Display #(.decimalPoint("false")) hex_digit_display_20 (.value(R3[15:12]));
  Hex_Digit_Display #(.decimalPoint("false")) hex_digit_display_21 (.value(R3[11:8]));
  Hex_Digit_Display #(.decimalPoint("false")) hex_digit_display_22 (.value(register_2_q[3:0]));
  D_Flip_Flop d_ff_3 (.D(d_ff_2_q), .clk(clk), .Q(fv), .reset(rst));  // open: Qn, preset
  Hex_Digit_Display #(.decimalPoint("false")) hex_digit_display_23 (.value(R3[7:4]));
  Hex_Digit_Display #(.decimalPoint("false")) hex_digit_display_24 (.value(R3[3:0]));
  IRDecoder irdecoder_1 (
    .IR({pci, IR_q}), .clk(clk), .rst(rst), .st(st), .mv(mv), .sub(irdecoder_1_sub), .ld(ld), .ldI(ldi),
    .Rs(irdecoder_1_rs), .Rd(irdecoder_1_rd), .halt(irdecoder_1_halt));
  regWE regwe_1 (
    .regWrite(and_4_out), .Rd(irdecoder_1_rd), .reg3WE(reg3WE), .reg2WE(reg2WE), .reg1WE(reg1WE),
    .reg0WE(reg0WE));
  and and_4 (and_4_out, fv, ~jmp, ~st);  // AND_Gate
  Hex_Digit_Display #(.decimalPoint("false")) hex_digit_display_25 (.value(cyclecounter_1_cycles[15:12]));
  CycleCounter cyclecounter_1 (.halt(irdecoder_1_halt), .clk(clk), .rst(rst), .cycles(cyclecounter_1_cycles));
  srcSel srcsel_1 (.R1(R1), .R2(R2), .sel(irdecoder_1_rd), .R3(R3), .R0(R0), .regOut(Rd));
  srcSel srcsel_2 (.R1(R1), .R2(R2), .sel(irdecoder_1_rs), .R3(R3), .R0(R0), .regOut(Rs));
  Hex_Digit_Display #(.decimalPoint("false")) hex_digit_display_26 (.value(cyclecounter_1_cycles[11:8]));
  Hex_Digit_Display #(.decimalPoint("false")) hex_digit_display_27 (.value(cyclecounter_1_cycles[7:4]));
  assign bit_extender_2_out = {{14{1'b0}}, irdecoder_1_rs};  // Bit_Extender bit_extender_2
  Hex_Digit_Display #(.decimalPoint("false")) hex_digit_display_28 (.value(cyclecounter_1_cycles[3:0]));
  Hex_Digit_Display #(.decimalPoint("false")) hex_digit_display_29 (.value({msb, addersubtractor_me_1_sum_4}));
  Bit_Extender #(.in_width(16), .out_width(7), .\type ("zero")) bit_extender_3 (.in(Rs), .out(RsLower));
  Hex_Digit_Display #(.decimalPoint("false")) hex_digit_display_30 (.value(addersubtractor_me_1_sum_3));
  Hex_Digit_Display #(.decimalPoint("false")) hex_digit_display_31 (.value(addersubtractor_me_1_sum_2));
  AdderSubtractor_Me addersubtractor_me_1 (
    .op(irdecoder_1_sub), .B(Rs), .A(Rd), .Overflow(addersubtractor_me_1_overflow),
    .Sum({msb, addersubtractor_me_1_sum_4, addersubtractor_me_1_sum_3, addersubtractor_me_1_sum_2, addersubtractor_me_1_sum}));
  Hex_Digit_Display #(.decimalPoint("false")) hex_digit_display_32 (.value(addersubtractor_me_1_sum));
  and and_5 (and_5_out, addersubtractor_me_1_overflow, and_4_out);
  Register #(.width(1)) register_3 (.D(1'b1), .en(and_5_out), .clk(clk), .Q(register_3_q), .clr(rst));
  LED led_1 (.in(register_3_q));
  WriteSelect writeselect_1 (
    .Rs(Rs), .RsExt(bit_extender_2_out), .mv(mv), .ldi(ldi), .ld(ld), .ldR(loadRes),
    .Sum({msb, addersubtractor_me_1_sum_4, addersubtractor_me_1_sum_3, addersubtractor_me_1_sum_2, addersubtractor_me_1_sum}),
    .Write(Write));

  // Notes on the sheet:
  //   R0
  //   Fetch
  //   R1
  //   Decode
  //   Execute
  //   R2
  //   Writeback
  //   R3
  //   Cycles
  //   Result
endmodule

module srcSel (
  input  [15:0] R0,
  input  [15:0] R1,
  input  [15:0] R2,
  input  [15:0] R3,
  input  [1:0] sel,
  output [15:0] regOut
);

  Multiplexer #(.select(2), .width(16)) multiplexer_1 (.in0(R0), .in1(R1), .in2(R2), .in3(R3), .out(regOut), .sel(sel));
endmodule

module regWE (
  input  regWrite,
  input  [1:0] Rd,
  output reg3WE,
  output reg2WE,
  output reg1WE,
  output reg0WE
);

  Demultiplexer #(.select(2)) demultiplexer_1 (
    .out0(reg0WE), .out1(reg1WE), .out2(reg2WE), .out3(reg3WE), .in(regWrite), .sel(Rd));
endmodule

module ProgramCounter (
  input  jmpn,
  input  jmp,
  input  neg,
  input  [5:0] pci,
  input  clk,
  input  rst,
  output [5:0] pc
);

  wire [5:0] adder_1_out, multiplexer_1_out;

  Adder #(.width(6)) adder_1 (.a(pc), .b(6'b000001), .out(adder_1_out), .cin(1'b0));  // open: cout
  Multiplexer #(.select(3), .width(6)) multiplexer_1 (
    .in0(adder_1_out), .in1(adder_1_out), .in2(pci), .in3(adder_1_out), .in4(adder_1_out), .in5(pci),
    .in6(pci), .in7(pci), .out(multiplexer_1_out), .sel({neg, jmp, jmpn}));
  Register #(.width(6)) register_1 (.D(multiplexer_1_out), .en(1'b1), .clk(clk), .Q(pc), .clr(rst));

  // Other names for the same wires on the sheet: Sum[5:0] = pc
endmodule

module IRDecoder (
  input  [7:0] IR,
  input  clk,
  input  rst,
  output st,
  output mv,
  output sub,
  output ld,
  output ldI,
  output [1:0] Rs,
  output [1:0] Rd,
  output halt
);

  wire and_1_out, and_2_out, and_3_out, and_4_out, and_5_out, and_6_out, and_7_out;

  and and_1 (and_1_out, ~IR[0], IR[1], IR[2], ~IR[3]);  // AND_Gate
  and and_2 (and_2_out, IR[0], ~IR[2], ~IR[3], IR[1]);  // AND_Gate
  and and_3 (and_3_out, IR[0], IR[1], IR[2], IR[3]);
  and and_4 (and_4_out, ~IR[0], IR[1], IR[2], IR[3]);  // AND_Gate
  and and_5 (and_5_out, IR[4], IR[5], IR[6], IR[7]);
  and and_6 (and_6_out, IR[0], IR[1], ~IR[2], IR[3]);  // AND_Gate
  and and_7 (and_7_out, and_1_out, and_5_out);
  D_Flip_Flop d_ff_1 (.D(and_6_out), .clk(clk), .Q(st), .reset(rst));  // open: Qn, preset
  D_Flip_Flop d_ff_2 (.D(and_1_out), .clk(clk), .Q(mv), .reset(rst));  // open: Qn, preset
  D_Flip_Flop d_ff_3 (.D(and_2_out), .clk(clk), .Q(sub), .reset(rst));  // open: Qn, preset
  D_Flip_Flop d_ff_4 (.D(and_3_out), .clk(clk), .Q(ld), .reset(rst));  // open: Qn, preset
  D_Flip_Flop d_ff_5 (.D(and_4_out), .clk(clk), .Q(ldI), .reset(rst));  // open: Qn, preset
  Register #(.width(2)) register_1 (.D(IR[5:4]), .en(1'b1), .clk(clk), .Q(Rs), .clr(rst));
  Register #(.width(2)) register_2 (.D(IR[7:6]), .en(1'b1), .clk(clk), .Q(Rd), .clr(rst));
  D_Flip_Flop d_ff_6 (.D(and_7_out), .clk(clk), .Q(halt), .reset(rst));  // open: Qn, preset
endmodule

module CycleCounter (
  input  halt,
  input  clk,
  input  rst,
  output [15:0] cycles
);

  wire t_ff_1_qn;
  wire [15:0] adder_1_out;

  T_Flip_Flop t_ff_1 (.T(halt), .clk(clk), .Qn(t_ff_1_qn), .reset(rst));  // open: Q, preset
  Adder #(.width(16)) adder_1 (.a(cycles), .b(16'h1), .out(adder_1_out), .cin(1'b0));  // open: cout
  Register #(.width(16)) register_1 (.D(adder_1_out), .en(t_ff_1_qn), .clk(clk), .Q(cycles), .clr(rst));

  // Other names for the same wires on the sheet: Sum[15:0] = cycles
endmodule

module WriteSelect (
  input  [15:0] Rs,
  input  [15:0] RsExt,
  input  mv,
  input  ldi,
  input  ld,
  input  [15:0] ldR,
  input  [15:0] Sum,
  output [15:0] Write
);

  Multiplexer #(.select(3), .width(16)) multiplexer_1 (
    .in0(Sum), .in1(ldR), .in2(RsExt), .in4(Rs), .out(Write), .sel({mv, ldi, ld}));  // open: in3, in5, in6, in7
endmodule

module FA0 (
  input  A,
  input  B,
  output S,
  output Cout
);

  wire nor_1_out;

  nor nor_1 (nor_1_out, A, B);
  and and_1 (Cout, A, B);
  nor nor_2 (S, nor_1_out, Cout);

  // Notes on the sheet:
  //   14 transistors
  //   1.75
  //   1
  //   Sydney Newmark
  //   FA0
  //   1
  //   2.75
  //   1.75
endmodule

module FA1 (
  input  A,
  input  B,
  output S,
  output Cout
);

  wire nand_1_out;

  or or_1 (Cout, A, B);
  nand nand_1 (nand_1_out, A, B);
  nand nand_2 (S, Cout, nand_1_out);

  // Notes on the sheet:
  //   14 transistors
  //   1.75
  //   1
  //   Sydney Newmark
  //   FA1
  //   1
  //   2.75
  //   1.75
endmodule

module FAopt1 (
  input  A,
  input  B,
  input  Cin,
  output S,
  output Cout
);

  wire nand_1_out, nand_2_out, nor_1_out, nor_2_out, nor_3_out, not_1_out, not_2_out;

  nor nor_1 (nor_1_out, A, B);
  not not_1 (not_1_out, nand_1_out);
  nand nand_1 (nand_1_out, B, A);
  nor nor_2 (nor_2_out, nor_1_out, not_1_out);
  nor nor_3 (nor_3_out, nor_2_out, Cin);
  nand nand_2 (nand_2_out, nor_2_out, Cin);
  not not_2 (not_2_out, nand_2_out);
  nor nor_4 (S, nor_3_out, not_2_out);
  nand nand_3 (Cout, nand_2_out, nand_1_out);

  // Notes on the sheet:
  //   1
  //   1
  //   0.75
  //   1
  //   32 transistors
  //   1
  //   1
  //   Sydney Newmark
  //   FAopt1
  //   1
  //   0.75
  //   1
  //   If Cin < 2.75, then 5.5, else Cin + 2.75
  //   If Cin < 2.75, then 4.75, else Cin + 2
endmodule

module FAopt2 (
  input  A,
  input  B,
  input  Cin,
  output S,
  output Cout
);

  wire and_1_out, nand_1_out, nand_2_out, nand_3_out, nor_1_out, nor_2_out, nor_3_out, not_1_out;

  nor nor_1 (nor_1_out, A, B);
  not not_1 (not_1_out, nand_1_out);
  nand nand_1 (nand_1_out, B, A);
  nand nand_2 (nand_2_out, B, Cin);
  nand nand_3 (nand_3_out, A, Cin);
  nor nor_2 (nor_2_out, nor_1_out, not_1_out);
  nor nor_3 (nor_3_out, nor_2_out, Cin);
  and and_1 (and_1_out, nor_2_out, Cin);
  nor nor_4 (S, nor_3_out, and_1_out);
  nand nand_4 (Cout, nand_1_out, nand_2_out, nand_3_out);

  // Notes on the sheet:
  //   1
  //   0.75
  //   1
  //   1
  //   1
  //   1
  //   42 transistors
  //   1
  //   1.75
  //   Sydney Newmark
  //   FAopt2
  //   1
  //   1.25
  //   Cin + 2.25
  //   If Cin < 2.75, then 5.5, else Cin + 2.75
endmodule

module RCA_4bit (
  input  [3:0] A,
  input  [3:0] B,
  output [3:0] S,
  output Cout
);

  wire fa0_1_cout, faopt1_2_cout, faopt2_1_cout;

  FAopt1 faopt1_1 (.A(A[3]), .B(B[3]), .Cin(faopt1_2_cout), .S(S[3]), .Cout(Cout));
  FAopt1 faopt1_2 (.A(A[2]), .B(B[2]), .Cin(faopt2_1_cout), .S(S[2]), .Cout(faopt1_2_cout));
  FAopt2 faopt2_1 (.A(A[1]), .B(B[1]), .Cin(fa0_1_cout), .S(S[1]), .Cout(faopt2_1_cout));
  FA0 fa0_1 (.A(A[0]), .B(B[0]), .S(S[0]), .Cout(fa0_1_cout));

  // Notes on the sheet:
  //   8
  //   8.25
  //   6
  //   6.75
  //   4
  //   5.5
  //   1.75
  //   2.75
  //   8
  //   8.25
endmodule

module RCA_4bit_0 (
  input  Cin,
  input  [3:0] A,
  input  [3:0] B,
  output [3:0] S,
  output Cout
);

  wire faopt1_2_cout, faopt1_3_cout, faopt2_1_cout;

  FAopt1 faopt1_1 (.A(A[3]), .B(B[3]), .Cin(faopt1_2_cout), .S(S[3]), .Cout(Cout));
  FAopt1 faopt1_2 (.A(A[2]), .B(B[2]), .Cin(faopt2_1_cout), .S(S[2]), .Cout(faopt1_2_cout));
  FAopt2 faopt2_1 (.A(A[1]), .B(B[1]), .Cin(faopt1_3_cout), .S(S[1]), .Cout(faopt2_1_cout));
  FAopt1 faopt1_3 (.A(B[0]), .B(A[0]), .Cin(Cin), .S(S[0]), .Cout(faopt1_3_cout));

  // Notes on the sheet:
  //   8
  //   8.75
  //   6
  //   6.75
  //   Sydney Newmark
  //   4-bit RCA FA0
  //   4
  //   5.5
  //   130 transistors
  //   1.75
  //   2.75
  //   8
  //   8.75
endmodule

module RCA_4bit_1 (
  input  [3:0] A,
  input  [3:0] B,
  output [3:0] S,
  output Cout
);

  wire fa1_1_cout, faopt1_2_cout, faopt2_1_cout;

  FAopt1 faopt1_1 (.A(A[3]), .B(B[3]), .Cin(faopt1_2_cout), .S(S[3]), .Cout(Cout));
  FAopt1 faopt1_2 (.A(A[2]), .B(B[2]), .Cin(faopt2_1_cout), .S(S[2]), .Cout(faopt1_2_cout));
  FAopt2 faopt2_1 (.A(A[1]), .B(B[1]), .Cin(fa1_1_cout), .S(S[1]), .Cout(faopt2_1_cout));
  FA1 fa1_1 (.A(A[0]), .B(B[0]), .S(S[0]), .Cout(fa1_1_cout));

  // Notes on the sheet:
  //   8
  //   8.75
  //   6
  //   6.75
  //   Sydney Newmark
  //   4-bit RCA FA1
  //   4
  //   5.5
  //   1.75
  //   2.75
  //   8
  //   8.75
endmodule

module RCA_8bit (
  input  [7:0] A,
  input  [7:0] B,
  output [7:0] S,
  output Cout
);

  wire fa0_1_cout, faopt1_2_cout, faopt1_3_cout, faopt1_4_cout, faopt1_5_cout, faopt1_6_cout, faopt2_1_cout;

  FAopt1 faopt1_1 (.A(A[7]), .B(B[7]), .Cin(faopt1_2_cout), .S(S[7]), .Cout(Cout));
  FAopt1 faopt1_2 (.A(A[6]), .B(B[6]), .Cin(faopt1_3_cout), .S(S[6]), .Cout(faopt1_2_cout));
  FAopt1 faopt1_3 (.A(A[5]), .B(B[5]), .Cin(faopt1_4_cout), .S(S[5]), .Cout(faopt1_3_cout));
  FAopt1 faopt1_4 (.A(A[4]), .B(B[4]), .Cin(faopt1_5_cout), .S(S[4]), .Cout(faopt1_4_cout));
  FAopt1 faopt1_5 (.A(A[3]), .B(B[3]), .Cin(faopt1_6_cout), .S(S[3]), .Cout(faopt1_5_cout));
  FAopt1 faopt1_6 (.A(A[2]), .B(B[2]), .Cin(faopt2_1_cout), .S(S[2]), .Cout(faopt1_6_cout));
  FAopt2 faopt2_1 (.A(A[1]), .B(B[1]), .Cin(fa0_1_cout), .S(S[1]), .Cout(faopt2_1_cout));
  FA0 fa0_1 (.A(A[0]), .B(B[0]), .S(S[0]), .Cout(fa0_1_cout));

  // Notes on the sheet:
  //   14
  //   16.75
  //   12
  //   14.75
  //   6 FAs excluding FAopt2 and FA0
  //   4 new FAs
  //   8+(4 * 2) = 16 (cout)
  //   16 + .75 = 16.75 (sum)
  //   10
  //   12.75
  //   10.75
  //   Sydney Newmark
  //   8-bit RCA
  //   8
  //   6
  //   8.75
  //   248 transistors
  //   4
  //   6.75
  //   5.5
  //   1.75
  //   2.75
  //   16
  //   16.75
endmodule

module CSA_8bit_0 (
  input  cin,
  input  [7:0] a,
  input  [7:0] b,
  output [7:0] s,
  output Cout
);

  wire mux_2x1_alt_1_x1, rca_4bit_0_1_cout, rca_4bit_0_2_cout, rca_4bit_1_1_cout;
  wire [3:0] mx2i_4_1_out_4, rca_4bit_0_1_s, rca_4bit_1_1_s;

  RCA_4bit_1 rca_4bit_1_1 (.A(a[7:4]), .B(b[7:4]), .S(rca_4bit_1_1_s), .Cout(rca_4bit_1_1_cout));
  Mux_2x1_alt mux_2x1_alt_1 (
    .in0(rca_4bit_0_1_cout), .in1(rca_4bit_1_1_cout), .sel(rca_4bit_0_2_cout), .x1(mux_2x1_alt_1_x1));
  mx2i_4 mx2i_4_1 (.in0(rca_4bit_0_1_s), .in1(rca_4bit_1_1_s), .sel(rca_4bit_0_2_cout), .out_4(mx2i_4_1_out_4));
  RCA_4bit_0 rca_4bit_0_1 (.Cin(1'b0), .A(a[7:4]), .B(b[7:4]), .S(rca_4bit_0_1_s), .Cout(rca_4bit_0_1_cout));
  not not_1 (Cout, mux_2x1_alt_1_x1);
  assign s[7:4] = ~mx2i_4_1_out_4;  // NOT_Gate not_2, 4 bits wide
  RCA_4bit_0 rca_4bit_0_2 (.Cin(cin), .A(a[3:0]), .B(b[3:0]), .S(s[3:0]), .Cout(rca_4bit_0_2_cout));

  // Notes on the sheet:
  //   8
  //   9.75
  //   8.75
  //   8
  //   9.75
  //   8.75
  //   8
  //   10.5
  //   8.75
  //   10.5
endmodule

module CSA_8bit_1 (
  input  [7:0] a,
  input  [7:0] b,
  output [7:0] s,
  output Cout
);

  wire mux_2x1_alt_1_x1, rca_4bit_0_1_cout, rca_4bit_1_1_cout, rca_4bit_1_2_cout;
  wire [3:0] mx2i_4_1_out_4, rca_4bit_0_1_s, rca_4bit_1_1_s;

  RCA_4bit_1 rca_4bit_1_1 (.A(a[7:4]), .B(b[7:4]), .S(rca_4bit_1_1_s), .Cout(rca_4bit_1_1_cout));
  Mux_2x1_alt mux_2x1_alt_1 (
    .in0(rca_4bit_0_1_cout), .in1(rca_4bit_1_1_cout), .sel(rca_4bit_1_2_cout), .x1(mux_2x1_alt_1_x1));
  mx2i_4 mx2i_4_1 (.in0(rca_4bit_0_1_s), .in1(rca_4bit_1_1_s), .sel(rca_4bit_1_2_cout), .out_4(mx2i_4_1_out_4));
  RCA_4bit_0 rca_4bit_0_1 (.A(a[7:4]), .B(b[7:4]), .S(rca_4bit_0_1_s), .Cout(rca_4bit_0_1_cout));  // open: Cin
  not not_1 (Cout, mux_2x1_alt_1_x1);
  assign s[7:4] = ~mx2i_4_1_out_4;  // NOT_Gate not_2, 4 bits wide
  RCA_4bit_1 rca_4bit_1_2 (.A(a[3:0]), .B(b[3:0]), .S(s[3:0]), .Cout(rca_4bit_1_2_cout));
endmodule

module CSA_16bit (
  input  cin,
  input  [15:0] a,
  input  [15:0] b,
  output [15:0] s,
  output Cout
);

  wire csa_8bit_0_1_cout, csa_8bit_0_2_cout, csa_8bit_1_1_cout, mux_2x1_alt_1_x1;
  wire [7:0] csa_8bit_0_1_s, csa_8bit_1_1_s, mx2i_8_1_o;

  CSA_8bit_1 csa_8bit_1_1 (.a(a[15:8]), .b(b[15:8]), .Cout(csa_8bit_1_1_cout), .s(csa_8bit_1_1_s));
  Mux_2x1_alt mux_2x1_alt_1 (
    .in0(csa_8bit_0_1_cout), .in1(csa_8bit_1_1_cout), .sel(csa_8bit_0_2_cout), .x1(mux_2x1_alt_1_x1));
  mx2i_8 mx2i_8_1 (.s(csa_8bit_0_2_cout), .in0(csa_8bit_0_1_s), .in1(csa_8bit_1_1_s), .o(mx2i_8_1_o));
  not not_1 (Cout, mux_2x1_alt_1_x1);
  CSA_8bit_0 csa_8bit_0_1 (.cin(1'b0), .a(a[15:8]), .b(b[15:8]), .Cout(csa_8bit_0_1_cout), .s(csa_8bit_0_1_s));
  assign s[15:8] = ~mx2i_8_1_o;  // NOT_Gate not_2, 8 bits wide
  CSA_8bit_0 csa_8bit_0_2 (.cin(cin), .a(a[7:0]), .b(b[7:0]), .Cout(csa_8bit_0_2_cout), .s(s[7:0]));

  // Notes on the sheet:
  //   10.5
  //   12.25
  //   10.5
  //   10.5
  //   Sydney Newmark
  //   16-bit Carry Select Adder
  //   12.25
  //   10.5
  //   13
  //   10.5
  //   8 new FAs
  //   16+(8 * 2) = 32 (cout)
  //   10.5
  //   Comparison to a 16-bit RCA
  //   14 FAs excluding FAopt2 and FA0
  //   32 + .75 = 32.75 (sum)
  //   13
endmodule

module Mux_2x1 (
  input  in0,
  input  s,
  input  in1,
  output z
);

  wire nand_1_out, nand_2_out, not_1_out;

  not not_1 (not_1_out, s);
  nand nand_1 (nand_1_out, in0, not_1_out);
  nand nand_2 (nand_2_out, in1, s);
  nand nand_3 (z, nand_1_out, nand_2_out);

  // Notes on the sheet:
  //   1
  //   0.75
  //   1
  //   2to1Mux
  //   Sydney Newmark
  //   1
  //   14 transistors
  //   z = max(s+2.75, in0+2, in1+2)
endmodule

module Mux_4x1 (
  input  in0,
  input  in1,
  input  in2,
  input  s1,
  input  in3,
  input  s0,
  output z
);

  wire mux_2x1_1_z, mux_2x1_2_z;

  Mux_2x1 mux_2x1_1 (.in0(in0), .s(s0), .in1(in1), .z(mux_2x1_1_z));
  Mux_2x1 mux_2x1_2 (.in0(in2), .s(s0), .in1(in3), .z(mux_2x1_2_z));
  Mux_2x1 mux_2x1_3 (.in0(mux_2x1_1_z), .s(s1), .in1(mux_2x1_2_z), .z(z));

  // Notes on the sheet:
  //   4to1 Mux
  //   Sydney Newmark
  //   42 transistors
  //   z= max(s0+4.75, s1+2.75, in0+4, in1+4, in2+4, in3+4)
endmodule

module Mux_2x1_alt (
  input  in0,
  input  in1,
  input  sel,
  output x1
);

  wire transmission_1_p3, transmission_1_p4;

  // Transmission_Gate transmission_1: pin names not known; wires that end beside it: in0, sel, transmission_1_p3, transmission_1_p4
  not not_1 (transmission_1_p3, sel);
  // Transmission_Gate transmission_2: pin names not known; wires that end beside it: in1, transmission_1_p3, sel, transmission_1_p4
  not not_2 (x1, transmission_1_p4);

  // Notes on the sheet:
  //   0.25
  //   0.75
  //   0.25
  //   0.75
  //   2to1 Mux - Transmission Gates
  //   Sydney Newmark
  //   8 transistors
  //   x1 = max(sel+1.75, in0+1, in1+1)
endmodule

module Mux_4x1_alt (
  input  in0,
  input  in1,
  input  in2,
  input  s1,
  input  in3,
  input  s0,
  output z
);

  wire mux_2x1_alt_1_x1, mux_2x1_alt_2_x1;

  Mux_2x1_alt mux_2x1_alt_1 (.in0(in0), .in1(in1), .sel(s0), .x1(mux_2x1_alt_1_x1));
  Mux_2x1_alt mux_2x1_alt_2 (.in0(in2), .in1(in3), .sel(s0), .x1(mux_2x1_alt_2_x1));
  Mux_2x1_alt mux_2x1_alt_3 (.in0(mux_2x1_alt_1_x1), .in1(mux_2x1_alt_2_x1), .sel(s1), .x1(z));

  // Notes on the sheet:
  //   24 transistors
  //   4to1 Mux - Transmission Gates
  //   Sydney Newmark
  //   z= max(s0+2.75, s1+1.75, in0+2, in1+2, in2+2, in3+2)
endmodule

module mx2i_4 (
  input  [3:0] in0,
  input  [3:0] in1,
  input  sel,
  output [3:0] out_4
);

  Mux_2x1_alt mux_2x1_alt_1 (.in0(in0[0]), .in1(in1[0]), .sel(sel), .x1(out_4[0]));
  Mux_2x1_alt mux_2x1_alt_2 (.in0(in0[1]), .in1(in1[1]), .sel(sel), .x1(out_4[1]));
  Mux_2x1_alt mux_2x1_alt_3 (.in0(in0[2]), .in1(in1[2]), .sel(sel), .x1(out_4[2]));
  Mux_2x1_alt mux_2x1_alt_4 (.in0(in0[3]), .in1(in1[3]), .sel(sel), .x1(out_4[3]));

  // Notes on the sheet:
  //   z = max(sel+1.75, in0+1, in1+1)
  //   o = max(z0, z1, z2, z3)
endmodule

module mx2i_8 (
  input  [7:0] in0,
  input  [7:0] in1,
  input  s,
  output [7:0] o
);

  mx2i_4 mx2i_4_1 (.in0(in0[3:0]), .in1(in1[3:0]), .sel(s), .out_4(o[3:0]));
  mx2i_4 mx2i_4_2 (.in0(in0[7:4]), .in1(in1[7:4]), .sel(s), .out_4(o[7:4]));

  // Notes on the sheet:
  //   z = max(z0, z1, z2, z3)
  //   o = max(z0, z1)
endmodule

module AOI21 (
  input  B,
  input  C,
  input  A,
  output O
);

  wire transistor_2_out, transistor_6_out;

  Transistor #(.\type ("n")) transistor_1 (.in(1'b0), .out(O), .gate(A));
  Transistor transistor_2 (.in(1'b1), .out(transistor_2_out), .gate(B));
  Transistor transistor_3 (.in(transistor_2_out), .out(O), .gate(A));
  Transistor transistor_4 (.in(1'b1), .out(transistor_2_out), .gate(C));
  Transistor #(.\type ("n")) transistor_5 (.in(transistor_6_out), .out(O), .gate(C));
  Transistor #(.\type ("n")) transistor_6 (.in(1'b0), .out(transistor_6_out), .gate(B));
endmodule

module C4_2 (
  input  C0,
  input  P0,
  input  P1,
  input  P2,
  input  P3,
  input  G0,
  input  G1,
  input  G2,
  input  G3,
  output C4
);

  wire nand_1_out, nand_2_out, nand_3_out, nand_4_out, nand_5_out, nor_1_out, nor_2_out, not_1_out,
       not_2_out, not_3_out, not_4_out;

  not not_1 (not_1_out, nand_1_out);
  nand nand_1 (nand_1_out, P1, P2, P3);
  nand nand_2 (nand_2_out, G2, P3);
  nand nand_3 (nand_3_out, G1, P2, P3);
  nand nand_4 (nand_4_out, C0, P0, not_1_out);
  not not_2 (not_2_out, nand_2_out);
  nand nand_5 (nand_5_out, G0, not_1_out);
  nor nor_1 (nor_1_out, G3, not_2_out);
  not not_3 (not_3_out, nand_5_out);
  not not_4 (not_4_out, nand_4_out);
  nor nor_2 (nor_2_out, not_3_out, not_4_out);
  nand nand_6 (C4, nor_1_out, nand_3_out, nor_2_out);
endmodule

module C4_3 (
  input  C0,
  input  P0,
  input  P1,
  input  P2,
  input  P3,
  input  G0,
  input  G1,
  input  G2,
  input  G3,
  output C4
);

  wire aoi21_1_o, nand_1_out, nand_2_out, nand_3_out, nand_4_out, nor_1_out, nor_2_out, nor_3_out, nor_4_out,
       not_1_out, not_2_out, not_3_out, not_4_out;

  not not_1 (not_1_out, G0);
  nand nand_1 (nand_1_out, P1, P2, P3);
  not not_2 (not_2_out, P0);
  nand nand_2 (nand_2_out, P3, G2);
  nand nand_3 (nand_3_out, G1, P2, P3);
  nor nor_1 (nor_1_out, not_1_out, nand_1_out);
  not not_3 (not_3_out, nand_3_out);
  not not_4 (not_4_out, nand_2_out);
  nor nor_2 (nor_2_out, not_2_out, nand_1_out);
  nor nor_3 (nor_3_out, G3, not_4_out);
  nor nor_4 (nor_4_out, not_3_out, nor_1_out);
  nand nand_4 (nand_4_out, nor_3_out, nor_4_out);
  AOI21 aoi21_1 (.A(nand_4_out), .B(nor_2_out), .C(C0), .O(aoi21_1_o));
  not not_5 (C4, aoi21_1_o);

  // Notes on the sheet:
  //   Worst Case: 2
  //   1.25
  //   0.75
endmodule

module AdderSubtractor_Logisim (
  input  Op,
  input  [15:0] A,
  input  [15:0] B,
  output [15:0] Sum,
  output Cout,
  output Overflow
);

  wire nor_1_out, nor_2_out, nor_3_out, nor_4_out, nor_5_out, nor_6_out, not_2_out, not_3_out, not_4_out,
       not_5_out;
  wire [15:0] multiplexer_1_out, not_1_out;

  Multiplexer #(.width(16)) multiplexer_1 (.in0(B), .in1(not_1_out), .out(multiplexer_1_out), .sel(Op));
  assign not_1_out = ~B;  // NOT_Gate not_1, 16 bits wide
  not not_2 (not_2_out, A[15]);
  nor nor_1 (nor_1_out, not_2_out, not_3_out);
  not not_3 (not_3_out, multiplexer_1_out[15]);
  nor nor_2 (nor_2_out, multiplexer_1_out[15], A[15]);
  Adder #(.width(16)) adder_1 (.a(A), .b(multiplexer_1_out), .out(Sum), .cin(Op), .cout(Cout));
  nor nor_3 (nor_3_out, nor_1_out, nor_2_out);
  not not_4 (not_4_out, Sum[15]);
  not not_5 (not_5_out, A[15]);
  nor nor_4 (nor_4_out, not_4_out, A[15]);
  nor nor_5 (nor_5_out, not_5_out, Sum[15]);
  nor nor_6 (nor_6_out, nor_4_out, nor_5_out);
  nor nor_7 (Overflow, nor_3_out, nor_6_out);

  // Notes on the sheet:
  //   -1, -1, no overflow
  //   32767, -1, sub overflow
  //   32767, 1, add overflow
  //   -21771, 24490, sub overflow
endmodule

module AdderSubtractor_Me (
  input  [15:0] B,
  input  [15:0] A,
  input  op,
  output [15:0] Sum,
  output Overflow
);

  wire nor_1_out, nor_2_out, nor_3_out, nor_4_out, nor_5_out, nor_6_out, not_2_out, not_3_out, not_4_out,
       not_5_out;
  wire [15:0] multiplexer_1_out, not_1_out;

  assign not_1_out = ~B;  // NOT_Gate not_1, 16 bits wide
  Multiplexer #(.width(16)) multiplexer_1 (.in0(B), .in1(not_1_out), .out(multiplexer_1_out), .sel(op));
  not not_2 (not_2_out, A[15]);
  not not_3 (not_3_out, multiplexer_1_out[15]);
  nor nor_1 (nor_1_out, multiplexer_1_out[15], A[15]);
  CSA_16bit csa_16bit_1 (.cin(op), .a(A), .b(multiplexer_1_out), .s(Sum));  // open: Cout
  nor nor_2 (nor_2_out, not_2_out, not_3_out);
  nor nor_3 (nor_3_out, nor_2_out, nor_1_out);
  not not_4 (not_4_out, Sum[15]);
  not not_5 (not_5_out, A[15]);
  nor nor_4 (nor_4_out, not_4_out, A[15]);
  nor nor_5 (nor_5_out, not_5_out, Sum[15]);
  nor nor_6 (nor_6_out, nor_4_out, nor_5_out);
  nor nor_7 (Overflow, nor_3_out, nor_6_out);
endmodule
